// Logisim project RAM_frase.circ as structural Verilog: 1 circuit, main circuit main
module main (
  input  [7:0] in_1,
  input  in_2,
  input  in_3,
  input  in_4,
  output [7:0] out_5
);

  wire comparator_1_eq, keyboard_1_avail;
  wire [6:0] keyboard_1_data;

  Clock clock_1 ();  // open: out
  Counter counter_1 (.count(in_3), .Q(out_5), .clk(in_2), .clr(comparator_1_eq));  // open: load, D, carry
  Keyboard #(.trigger("falling")) keyboard_1 (
    .clk(in_2), .re(in_3), .clr(in_4), .avail(keyboard_1_avail), .data(keyboard_1_data));
  Comparator comparator_1 (.a(out_5), .b(in_1), .eq(comparator_1_eq));  // open: gt, lt
  RAM #(.dataWidth(7), .bus("separate")) ram_1 (
    .addr(out_5), .din(keyboard_1_data), .str(keyboard_1_avail), .sel(in_3), .clk(in_2), .ld(in_2),
    .clr(comparator_1_eq));  // open: data
  TTY tty_1 (.data(keyboard_1_data), .clk(in_2), .clr(comparator_1_eq));  // open: we
endmodule
