// Logisim project ROM_frase.circ as structural Verilog: 1 circuit, main circuit main
module main (
  input  in_1,
  input  [7:0] in_2
);

  wire clock_1_out, comparator_1_eq;
  wire [6:0] rom_1_data;
  wire [7:0] counter_1_q;

  Clock clock_1 (.out(clock_1_out));
  Counter counter_1 (.count(in_1), .Q(counter_1_q), .clk(clock_1_out), .clr(comparator_1_eq));  // open: load, D, carry
  Comparator comparator_1 (.a(counter_1_q), .b(in_2), .eq(comparator_1_eq));  // open: gt, lt
  ROM #(.dataWidth(7)) rom_1 (.addr(counter_1_q), .data(rom_1_data));  // open: sel
  TTY tty_1 (.data(rom_1_data), .clk(clock_1_out), .clr(comparator_1_eq));  // open: we

  // Notes on the sheet:
  //   contents of rom_1 (hex, n*v repeats v):
  //   48 45 4c 4c 4f 20 57 4f 52 4c 44
endmodule
