// Logisim project calculadora_simples_2.circ as structural Verilog: 1 circuit, main circuit main
module main (
  input  in_1,
  input  in_2,
  input  in_3,
  input  [7:0] _0000001,
  input  _1,
  input  _1_2,
  input  [6:0] in_7,
  input  [6:0] in_8,
  input  [6:0] _0101101,
  input  [6:0] in_10,
  input  [6:0] in_11,
  input  _1_3,
  input  [7:0] in_13,
  input  _1_4,
  output [6:0] out_15,
  output [6:0] out_16,
  output [6:0] out_17,
  output [6:0] out_18,
  output [6:0] out_19,
  output out_20,
  output [1:0] out_21
);

  wire comparator_1_eq, comparator_2_eq, comparator_3_eq, comparator_4_eq, keyboard_1_avail, not_1_out,
       undriven;
  wire [6:0] adder_1_out, divider_1_out, keyboard_1_data, multiplier_1_out, register_1_q, register_2_q,
       subtractor_3_out;
  wire [7:0] counter_1_q;

  not not_1 (not_1_out, in_1);
  Keyboard keyboard_1 (.clk(in_1), .re(in_2), .clr(in_3), .avail(keyboard_1_avail), .data(keyboard_1_data));
  Counter counter_1 (.D(_0000001), .count(_1), .Q(counter_1_q), .clk(not_1_out), .clr(in_3));  // open: load, carry
  Comparator #(.width(7)) comparator_1 (.a(in_7), .b(out_16), .eq(comparator_1_eq));  // open: gt, lt
  Comparator #(.width(7)) comparator_2 (.a(_0101101), .b(out_16), .eq(comparator_2_eq));  // open: gt, lt
  Comparator #(.width(7)) comparator_3 (.a(in_10), .b(out_16), .eq(comparator_3_eq));  // open: gt, lt
  Comparator #(.width(7)) comparator_4 (.a(in_11), .b(out_16), .eq(comparator_4_eq));  // open: gt, lt
  Comparator comparator_5 (.a(in_13), .b(counter_1_q), .eq(out_20));  // open: gt, lt
  Register #(.width(7)) register_1 (
    .D(keyboard_1_data), .en(keyboard_1_avail), .Q(register_1_q), .clk(in_1), .clr(in_3));
  Priority_Encoder #(.select(2)) priority_encoder_1 (
    .in0(comparator_1_eq), .in1(comparator_2_eq), .in2(comparator_3_eq), .in3(comparator_4_eq), .out(out_21),
    .en_in(_1_3));  // open: gs, en_out
  Register #(.width(7)) register_2 (.D(register_1_q), .Q(register_2_q), .clk(in_1), .clr(in_3));  // open: en
  Register #(.width(7)) register_3 (.D(register_2_q), .Q(out_16), .clk(in_1), .clr(in_3));  // open: en
  Subtractor #(.width(7)) subtractor_1 (.a(register_2_q), .b(in_8), .out(out_18));  // open: bin, bout
  Subtractor #(.width(7)) subtractor_2 (.a(register_1_q), .b(in_8), .out(out_17));  // open: bin, bout
  Adder #(.width(7)) adder_1 (.a(out_18), .b(out_17), .out(adder_1_out), .cin(undriven));  // open: cout
  Subtractor #(.width(7)) subtractor_3 (.a(out_18), .b(out_17), .out(subtractor_3_out));  // open: bin, bout
  Multiplier #(.width(7)) multiplier_1 (.a(out_18), .b(out_17), .out(multiplier_1_out));  // open: cin, cout
  Divider #(.width(7)) divider_1 (.a(out_18), .b(out_17), .out(divider_1_out));  // open: upper, rem
  Adder #(.width(7)) adder_2 (.a(out_19), .b(in_8), .out(out_15));  // open: cin, cout
  Multiplexer #(.select(2), .width(7)) multiplexer_1 (
    .in0(adder_1_out), .in1(subtractor_3_out), .in2(multiplier_1_out), .in3(divider_1_out), .out(out_19),
    .sel(out_21), .en(_1_4));
  TTY tty_1 (.data(out_15), .clk(out_20), .we(_1_2), .clr(in_3));

  // Notes on the sheet:
  //   0101011
  //   0101010
  //   0111101
  //   00000011
  //   0110000
endmodule
