// Logisim project calculadora_simples.circ as structural Verilog: 1 circuit, main circuit main
module main (
  input  in_1,
  input  in_2,
  input  in_3,
  input  in_4,
  input  in_5,
  input  in_6,
  input  [6:0] in_7,
  input  in_8,
  input  [6:0] in_9,
  input  [6:0] in_10,
  input  [6:0] in_11,
  input  [6:0] in_12,
  input  in_13,
  input  in_14,
  output [6:0] out_15,
  output [1:0] out_16
);

  wire comparator_1_eq, comparator_2_eq, comparator_3_eq, comparator_4_eq, keyboard_1_avail, undriven;
  wire [6:0] adder_1_out, adder_2_out, divider_1_out, keyboard_1_data, multiplexer_1_out, multiplier_1_out,
       register_1_q, register_2_q, subtractor_1_out, subtractor_2_out, subtractor_3_out;

  Keyboard keyboard_1 (.clk(in_1), .re(in_2), .clr(in_3), .avail(keyboard_1_avail), .data(keyboard_1_data));
  Comparator #(.width(7)) comparator_1 (.a(in_7), .b(out_15), .eq(comparator_1_eq));  // open: gt, lt
  Comparator #(.width(7)) comparator_2 (.a(in_10), .b(out_15), .eq(comparator_2_eq));  // open: gt, lt
  Comparator #(.width(7)) comparator_3 (.a(in_11), .b(out_15), .eq(comparator_3_eq));  // open: gt, lt
  Comparator #(.width(7)) comparator_4 (.a(in_12), .b(out_15), .eq(comparator_4_eq));  // open: gt, lt
  Comparator comparator_5 ();  // open: a, b, gt, eq, lt
  Register #(.width(7)) register_1 (
    .D(keyboard_1_data), .en(keyboard_1_avail), .Q(register_1_q), .clk(in_1), .clr(in_5));
  Register #(.width(7)) register_2 (.D(register_1_q), .Q(register_2_q), .clk(in_1), .clr(in_5));  // open: en
  Priority_Encoder #(.select(2)) priority_encoder_1 (
    .in0(comparator_1_eq), .in1(comparator_2_eq), .in2(comparator_3_eq), .in3(comparator_4_eq), .out(out_16),
    .en_in(in_13));  // open: gs, en_out
  Register #(.width(7)) register_3 (.D(register_2_q), .Q(out_15), .clk(in_1), .clr(in_5));  // open: en
  Subtractor #(.width(7)) subtractor_1 (.a(register_2_q), .b(in_9), .out(subtractor_1_out));  // open: bin, bout
  Subtractor #(.width(7)) subtractor_2 (.a(register_1_q), .b(in_9), .out(subtractor_2_out));  // open: bin, bout
  Adder #(.width(7)) adder_1 (
    .a(subtractor_1_out), .b(subtractor_2_out), .out(adder_1_out), .cin(undriven));  // open: cout
  Subtractor #(.width(7)) subtractor_3 (
    .a(subtractor_1_out), .b(subtractor_2_out), .out(subtractor_3_out));  // open: bin, bout
  Multiplier #(.width(7)) multiplier_1 (
    .a(subtractor_1_out), .b(subtractor_2_out), .out(multiplier_1_out));  // open: cin, cout
  Divider #(.width(7)) divider_1 (.a(subtractor_1_out), .b(subtractor_2_out), .out(divider_1_out));  // open: upper, rem
  Adder #(.width(7)) adder_2 (.a(multiplexer_1_out), .b(in_9), .out(adder_2_out));  // open: cin, cout
  Multiplexer #(.select(2), .width(7)) multiplexer_1 (
    .in0(adder_1_out), .in1(subtractor_3_out), .in2(multiplier_1_out), .in3(divider_1_out),
    .out(multiplexer_1_out), .sel(out_16), .en(in_14));
  TTY tty_1 (.data(adder_2_out), .clk(in_4), .we(in_6), .clr(in_8));
endmodule
