// Logisim project ULA_com_ROM.circ as structural Verilog: 1 circuit, main circuit main
module main (
  input  in_1,
  input  A,
  input  B,
  input  default__1,
  input  default__1_2,
  input  [1:0] F1___F2,
  input  default__1_3,
  output out_8,
  output [1:0] out_9,
  output out_10
);

  wire and_1_out, and_2_out, and_3_out, and_4_out, and_5_out, and_6_out, and_7_out, demultiplexer_1_out0,
       demultiplexer_1_out1, demultiplexer_1_out2, demultiplexer_1_out3, not_1_out, or_1_out, or_4_out,
       xor_1_out;

  ROM #(.addrWidth(2), .dataWidth(2)) rom_1 (.addr(F1___F2), .data(out_9), .sel(default__1_3));
  Demultiplexer #(.select(2)) demultiplexer_1 (
    .out0(demultiplexer_1_out0), .out1(demultiplexer_1_out1), .out2(demultiplexer_1_out2),
    .out3(demultiplexer_1_out3), .in(default__1), .sel(out_9), .en(default__1_2));
  and and_1 (and_1_out, A, B);
  or or_1 (or_1_out, A, B);
  not not_1 (not_1_out, B);
  and and_2 (and_2_out, and_1_out, demultiplexer_1_out0);
  and and_3 (and_3_out, or_1_out, demultiplexer_1_out1);
  and and_4 (and_4_out, not_1_out, demultiplexer_1_out2);
  and and_5 (and_5_out, demultiplexer_1_out3, B, A);
  or or_2 (out_10, and_5_out, and_6_out);
  xor xor_1 (xor_1_out, B, A);
  and and_6 (and_6_out, demultiplexer_1_out3, xor_1_out, in_1);
  or or_3 (out_8, and_2_out, and_3_out, and_4_out, and_7_out);
  or or_4 (or_4_out, in_1, xor_1_out);
  and and_7 (and_7_out, or_4_out, demultiplexer_1_out3);

  // Notes on the sheet:
  //   valores: 0 1 2 3
  //   contents of rom_1 (hex, n*v repeats v):
  //   0 1 2 3
endmodule
