// Logisim project ULA_sem_ROM.circ as structural Verilog: 1 circuit, main circuit main
module main (
  input  in_1,
  input  A,
  input  B,
  input  F0,
  input  F1,
  output out_6,
  output out_7
);

  wire and_1_out, and_2_out, and_3_out, and_4_out, and_5_out, and_6_out, and_7_out, and_8_out, and_9_out,
       and_10_out, and_11_out, not_1_out, not_2_out, not_3_out, not_4_out, not_5_out, or_1_out, or_3_out,
       xor_1_out;

  not not_1 (not_1_out, F0);
  and and_1 (and_1_out, A, B);
  or or_1 (or_1_out, A, B);
  not not_2 (not_2_out, B);
  not not_3 (not_3_out, F1);
  not not_4 (not_4_out, F0);
  not not_5 (not_5_out, F1);
  and and_2 (and_2_out, not_1_out, not_3_out);
  and and_3 (and_3_out, not_4_out, F1);
  and and_4 (and_4_out, F0, not_5_out);
  and and_5 (and_5_out, F0, F1);
  and and_6 (and_6_out, and_1_out, and_2_out);
  and and_7 (and_7_out, or_1_out, and_3_out);
  and and_8 (and_8_out, not_2_out, and_4_out);
  and and_9 (and_9_out, and_5_out, B, A);
  or or_2 (out_7, and_9_out, and_10_out);
  xor xor_1 (xor_1_out, B, A);
  and and_10 (and_10_out, and_5_out, xor_1_out, in_1);
  or or_3 (or_3_out, in_1, xor_1_out);
  or or_4 (out_6, and_6_out, and_7_out, and_8_out, and_11_out);
  and and_11 (and_11_out, or_3_out, and_5_out);
endmodule
